# Fritzing sketch ProMiniTCotrolwithLEDshow (saved by Fritzing 0.9.3b)
perfboards: 1

parts:
  IC1 = DS1302 [package="DIP8 [THT]"]
  D1 = LTE-302 [package=lte-302]
  S1 = Square Pushbutton
  R1 = Temperature Sensor (Thermistor) [thermistor_type=NTC package=THT]
  BAT1 = Battery Holders [package=battcon_245mm_pth]
  Part1 = Arduino Pro Mini (5V)
  R2 = Resistor [tolerance=±5% resistance=10k package=THT]
  XTAL1 = CRYSTAL - kHz [frequency="32 kHz"]
  LED1 = 7-SEGMENT-4DIGIT [package=7-segment-4digit]
  R4 = Resistor [tolerance=±5% resistance=1k package=THT]
  R6 = Resistor [tolerance=±5% resistance=1k package=THT]
  R7 = Resistor [tolerance=±5% resistance=1k package=THT]
  R8 = Resistor [tolerance=±5% resistance=1k package=THT]

nets:
  N1: IC1.+V, R1.pin_1
  N2: IC1.X1_-_Crystal, XTAL1.pin_1
  N3: IC1.X2_-_Crystal, XTAL1.pin_0
  N4: IC1.0V, D1.A, BAT1.+
  N5: IC1.CE_-_Chip_Enable, Part1.D7
  N6: IC1.I/O_-_SPI_Data_In/Out, Part1.D6
  N7: IC1.SCLK_-_SPI_Clock, Part1.D5
  N8: IC1.Vbat_-_Backup_Supply, BAT1.-
  N9: D1.C, Part1.D3
  N10: S1.leg0, Part1.A3
  N11: R1.pin_0, Part1.A0, R2.Pin_1
  N12: Part1.A4, LED1.3
  N13: Part1.GND, R2.Pin_0
  N14: Part1.A2, LED1.9
  N15: Part1.A1, LED1.5
  N16: Part1.SCK, LED1.4
  N17: Part1.MISO, R6.Pin_1
  N18: Part1.MOSI, R4.Pin_1
  N19: Part1.D10, R8.Pin_1
  N20: Part1.D9, LED1.14
  N21: Part1.D8, LED1.15
  N22: Part1.D4, LED1.2
  N23: Part1.D2, LED1.1
  N24: Part1.TXO, R7.Pin_0
  N25: LED1.6, R7.Pin_1
  N26: LED1.11, R6.Pin_0
  N27: LED1.13, R4.Pin_0
  N28: LED1.16, R8.Pin_0
